// Logisim project NANO_3-bit_Parity.circ as structural Verilog: 2 circuits, main circuit 3-Input Odd Parity
module main (
  output out_1
);

  wire dip_7404_1_p2, dip_7404_1_p4, dip_7404_1_p6, dip_7404_2_p2, dip_7404_2_p4, dip_7404_2_p6,
       dip_7404_2_p8, dip_7410_1_p7, dip_7410_2_p1, dip_7410_2_p8, dip_7410_2_p10, dip_7432_1_p3,
       dip_7432_1_p6, nano_1_p2, nano_1_p3, nano_1_p4;

  // NANO nano_1: pin names not known; wires that end beside it: 1'b0, nano_1_p2, nano_1_p3, nano_1_p4, 1'b1, 1'b0, out_1
  // DIP_7404 dip_7404_1: pin names not known; wires that end beside it: nano_1_p2, dip_7404_1_p2, nano_1_p3, dip_7404_1_p4, nano_1_p4, dip_7404_1_p6, 1'b0, 1'b0, 1'b0
  // DIP_7410 dip_7410_1: pin names not known; wires that end beside it: nano_1_p2, dip_7404_1_p4, dip_7404_1_p2, nano_1_p3, dip_7404_1_p6, dip_7404_1_p6, dip_7410_1_p7, nano_1_p4, dip_7404_1_p2
  // DIP_7410 dip_7410_2: pin names not known; wires that end beside it: dip_7410_2_p1, nano_1_p4, nano_1_p3, 1'b0, 1'b0, 1'b0, dip_7404_1_p4, dip_7410_2_p8, nano_1_p2, dip_7410_2_p10, 1'b0, 1'b0, 1'b0
  // DIP_7404 dip_7404_2: pin names not known; wires that end beside it: dip_7410_1_p7, dip_7404_2_p2, dip_7410_2_p1, dip_7404_2_p4, dip_7410_2_p8, dip_7404_2_p6, dip_7410_2_p10, dip_7404_2_p8, 1'b0, 1'b0
  // DIP_7432 dip_7432_1: pin names not known; wires that end beside it: dip_7404_2_p2, dip_7404_2_p4, dip_7432_1_p3, dip_7432_1_p3, dip_7404_2_p6, dip_7432_1_p6, 1'b0, 1'b0, dip_7404_2_p8, dip_7432_1_p6, out_1

  // Notes on the sheet:
  //   3-Input Odd Parity with available ICs and NANO V3 Driver
endmodule

module _3_Input_Odd_Parity (
  input  [2:0] in_1,
  input  [2:0] in_2,
  output out_3,
  output out_4
);

  wire and_1_out, and_2_out, and_3_out, and_4_out, dip_7404_1_p2, dip_7404_1_p4, dip_7404_1_p6,
       dip_7404_2_p2, dip_7404_2_p4, dip_7404_2_p6, dip_7404_2_p8, dip_7410_1_p7, dip_7410_2_p1,
       dip_7410_2_p8, dip_7410_2_p10, dip_7432_1_p3, dip_7432_1_p6, not_1_out, not_2_out, not_3_out;

  not not_1 (not_1_out, in_1[2]);
  not not_2 (not_2_out, in_1[1]);
  not not_3 (not_3_out, in_1[0]);
  // DIP_7404 dip_7404_1: pin names not known; wires that end beside it: in_2[2], dip_7404_1_p2, in_2[1], dip_7404_1_p4, in_2[0], dip_7404_1_p6, 1'b0, 1'b0, 1'b0
  and and_1 (and_1_out, in_1[2], not_2_out, not_3_out);
  and and_2 (and_2_out, not_1_out, in_1[1], not_3_out);
  and and_3 (and_3_out, not_2_out, not_1_out, in_1[0]);
  and and_4 (and_4_out, in_1[0], in_1[1], in_1[2]);
  // DIP_7410 dip_7410_1: pin names not known; wires that end beside it: in_2[2], dip_7404_1_p4, dip_7404_1_p2, in_2[1], dip_7404_1_p6, dip_7404_1_p6, dip_7410_1_p7, in_2[0], dip_7404_1_p2
  // DIP_7410 dip_7410_2: pin names not known; wires that end beside it: dip_7410_2_p1, in_2[0], in_2[1], 1'b0, 1'b0, 1'b0, dip_7404_1_p4, dip_7410_2_p8, in_2[2], dip_7410_2_p10, 1'b0, 1'b0, 1'b0
  or or_1 (out_3, and_1_out, and_2_out, and_3_out, and_4_out);
  // DIP_7404 dip_7404_2: pin names not known; wires that end beside it: dip_7410_1_p7, dip_7404_2_p2, dip_7410_2_p1, dip_7404_2_p4, dip_7410_2_p8, dip_7404_2_p6, dip_7410_2_p10, dip_7404_2_p8, 1'b0, 1'b0
  // DIP_7432 dip_7432_1: pin names not known; wires that end beside it: dip_7404_2_p2, dip_7404_2_p4, dip_7432_1_p3, dip_7432_1_p3, dip_7404_2_p6, dip_7432_1_p6, 1'b0, 1'b0, dip_7404_2_p8, dip_7432_1_p6, out_4

  // Notes on the sheet:
  //   3-Input Odd Parity pure logic
  //   3-Input Odd Parity with available ICs
endmodule
